// Digital circuit RV5-PROCESSOR.dig as structural Verilog
module RV5_PROCESSOR (
  input  clock,
  input  TCK,
  input  TMS,
  input  RESET,
  input  TDI,
  output [6:0] opcode,
  output TDO
);

  wire addr_en, alu_mod, br_cond, branch_sel, capture_dr, capture_ir, csr_sel, dmi_busy_d, dmistat_en,
       ecall_sel, exit1_dr, exit1_ir, exit2_dr, exit2_ir, funct3, funct7, I_imm_sel, jal_sel, jalr_sel,
       ld_signext, mret_sel, not_1_out, or_1_out, pause_dr, pause_ir, ram_b, ram_h, ram_ren, ram_wen,
       reg_wen, run_test_idle, S_imm_sel, SB_imm_sel, select_dr_scan, select_ir_scan, shift_dr, shift_ir,
       test_logic_reset, U_imm_sel, UJ_imm_sel, update_dr, update_ir;
  wire [1:0] alu_a_sel, dmistat, dmistat_d, op, op_d, rv5_pcu_1_pc, update_dr_dmistat, update_dr_op, wb_sel;
  wire [2:0] alu_op;
  wire [3:0] lookuptable_1_out, state_q;
  wire [4:0] active_ir, active_ir_d, ir_shift_d, multiplexer_8_out, multiplexer_9_out, rd, rs1, rs2;
  wire [4:1] ir_shift;
  wire [6:0] addr, addr_d, update_dr_addr;
  wire [11:0] system_imm;
  wire [29:0] rv5_pcu_1_pc_2;
  wire [31:0] data, data_d, imm_32, mepc, mtvec, multiplexer_6_out, multiplexer_11_out, multiplexer_12_out,
       ra, ROM_d, rv5_csr_1_r_data, rv5_gpr_1_rb, rv5_memory_1_p5, rv5_memory_1_p13, update_dr_data;
  wire [31:2] add_1_s;
  wire [40:0] capture_dr_dr_shift_d, dr_shift, dr_shift_d;

  Register dmi_busy (.D(dmi_busy_d), .C(TCK), .en(update_dr));  // open: Q
  nor nor_1 (dmi_busy_d, dmistat[0], dmistat[1]);
  not not_1 (not_1_out, TCK);
  Register tdo_latch (.D(dr_shift[0]), .C(not_1_out), .en(1'b1), .Q(TDO));
  Register #(.Bits(4)) state (.D(lookuptable_1_out), .C(clock), .en(1'b1), .Q(state_q));
  Decoder #(.Selector_Bits(4)) decoder_1 (
    .sel(state_q), .out_0(test_logic_reset), .out_1(run_test_idle), .out_2(select_dr_scan),
    .out_3(select_ir_scan), .out_4(capture_ir), .out_5(shift_ir), .out_6(exit1_ir), .out_7(pause_ir),
    .out_8(exit2_ir), .out_9(update_ir), .out_10(capture_dr), .out_11(shift_dr), .out_12(exit1_dr),
    .out_13(pause_dr), .out_14(exit2_dr), .out_15(update_dr));
  Register #(.Bits(2)) u_op (.D(op_d), .C(TCK), .en(addr_en), .Q(op));
  Register #(.Bits(7)) u_addr (.D(addr_d), .C(TCK), .en(addr_en), .Q(addr));
  Register #(.Bits(32)) u_data (.D(data_d), .C(TCK), .en(addr_en), .Q(data));
  Register #(.Bits(2)) u_dmistat (.D(dmistat_d), .C(TCK), .en(dmistat_en), .Q(dmistat));
  Register #(.Bits(5)) u_active_ir (.D(active_ir_d), .C(TCK), .en(1'b1), .Q(active_ir));
  Register #(.Bits(5)) u_ir_shift (.D(ir_shift_d), .C(TCK), .en(1'b1), .Q({ir_shift, dr_shift[0]}));
  Register #(.Bits(41)) u_dr_shift (
    .D(dr_shift_d), .C(TCK), .en(1'b1), .Q({dr_shift[40:17], dmistat_en, dr_shift[15:0]}));
  LookUpTable #(.Bits(4)) lookuptable_1 (
    .in0(TMS), .in1(state_q[0]), .in2(state_q[1]), .in3(state_q[2]), .in4(state_q[3]), .out(lookuptable_1_out));
  Multiplexer #(.Selector_Bits(4), .Bits(5)) multiplexer_1 (
    .sel(state_q), .in_0({ir_shift, dr_shift[0]}), .in_1({ir_shift, dr_shift[0]}),
    .in_2({ir_shift, dr_shift[0]}), .in_3({ir_shift, dr_shift[0]}), .in_4(5'b00001), .in_5({TDI, ir_shift}),
    .in_6({ir_shift, dr_shift[0]}), .in_7({ir_shift, dr_shift[0]}), .in_8({ir_shift, dr_shift[0]}),
    .in_9({ir_shift, dr_shift[0]}), .in_10({ir_shift, dr_shift[0]}), .in_11({ir_shift, dr_shift[0]}),
    .in_12({ir_shift, dr_shift[0]}), .in_13({ir_shift, dr_shift[0]}), .in_14({ir_shift, dr_shift[0]}),
    .in_15({ir_shift, dr_shift[0]}), .out(ir_shift_d));
  Multiplexer #(.Selector_Bits(5), .Bits(41)) multiplexer_2 (
    .sel(active_ir), .in_0({41{1'b0}}), .in_1(41'h967), .in_2({41{1'b0}}), .in_3({41{1'b0}}),
    .in_4({41{1'b0}}), .in_5({41{1'b0}}), .in_6({41{1'b0}}), .in_7({41{1'b0}}), .in_8({41{1'b0}}),
    .in_9({41{1'b0}}), .in_10({41{1'b0}}), .in_11({41{1'b0}}), .in_12({41{1'b0}}), .in_13({41{1'b0}}),
    .in_14({41{1'b0}}), .in_15({41{1'b0}}), .in_16({29'h1, dmistat, 10'h71}), .in_17({addr, data, dmistat}),
    .in_18({41{1'b0}}), .in_19({41{1'b0}}), .in_20({41{1'b0}}), .in_21({41{1'b0}}), .in_22({41{1'b0}}),
    .in_23({41{1'b0}}), .in_24({41{1'b0}}), .in_25({41{1'b0}}), .in_26({41{1'b0}}), .in_27({41{1'b0}}),
    .in_28({41{1'b0}}), .in_29({41{1'b0}}), .in_30({41{1'b0}}), .in_31({41{1'b0}}),
    .out(capture_dr_dr_shift_d));
  Multiplexer #(.Selector_Bits(4), .Bits(5)) multiplexer_3 (
    .sel(state_q), .in_0(5'b00001), .in_1(active_ir), .in_2(active_ir), .in_3(active_ir), .in_4(active_ir),
    .in_5(active_ir), .in_6(active_ir), .in_7(active_ir), .in_8(active_ir), .in_9({ir_shift, dr_shift[0]}),
    .in_10(active_ir), .in_11(active_ir), .in_12(active_ir), .in_13(active_ir), .in_14(active_ir),
    .in_15(active_ir), .out(active_ir_d));
  RV5_PCU rv5_pcu_1 (
    .IMM_32(imm_32), .CLK(clock), .IS_BRANCH(branch_sel), .IS_JAL(jal_sel), .IS_JALR(jalr_sel),
    .COND_MET(br_cond), .ALU_OUT(rv5_memory_1_p5), .IS_ECALL(ecall_sel), .MTVEC(mtvec), .MEPC(mepc),
    .IS_MRET(mret_sel), .PC({rv5_pcu_1_pc_2, rv5_pcu_1_pc}));
  nor nor_2 (addr_en, dmistat[0], dmistat[1]);
  Multiplexer #(.Selector_Bits(4), .Bits(41)) multiplexer_4 (
    .sel(state_q), .in_0({dr_shift[40:17], dmistat_en, dr_shift[15:0]}),
    .in_1({dr_shift[40:17], dmistat_en, dr_shift[15:0]}),
    .in_2({dr_shift[40:17], dmistat_en, dr_shift[15:0]}),
    .in_3({dr_shift[40:17], dmistat_en, dr_shift[15:0]}),
    .in_4({dr_shift[40:17], dmistat_en, dr_shift[15:0]}),
    .in_5({dr_shift[40:17], dmistat_en, dr_shift[15:0]}),
    .in_6({dr_shift[40:17], dmistat_en, dr_shift[15:0]}),
    .in_7({dr_shift[40:17], dmistat_en, dr_shift[15:0]}),
    .in_8({dr_shift[40:17], dmistat_en, dr_shift[15:0]}),
    .in_9({dr_shift[40:17], dmistat_en, dr_shift[15:0]}), .in_10(capture_dr_dr_shift_d),
    .in_11({TDI, dr_shift[40:17], dmistat_en, dr_shift[15:1]}),
    .in_12({dr_shift[40:17], dmistat_en, dr_shift[15:0]}),
    .in_13({dr_shift[40:17], dmistat_en, dr_shift[15:0]}),
    .in_14({dr_shift[40:17], dmistat_en, dr_shift[15:0]}),
    .in_15({dr_shift[40:17], dmistat_en, dr_shift[15:0]}), .out(dr_shift_d));
  RV5_IMM rv5_imm_1 (
    .UJ_imm_sel(UJ_imm_sel), .I_imm_sel(I_imm_sel), .SB_imm_sel(SB_imm_sel), .S_imm_sel(S_imm_sel),
    .U_imm_sel(U_imm_sel), .INSTR_32(ROM_d), .imm(imm_32));
  ROM #(.AddrBits(10), .isProgramMemory("true"), .Bits(32)) ROM (.A(rv5_pcu_1_pc_2[9:0]), .sel(1'b1), .D(ROM_d));
  Add #(.Bits(30)) add_1 (.a(rv5_pcu_1_pc_2), .b({30{1'b0}}), .c_i(1'b1), .s(add_1_s));  // open: c_o
  RV5_CSR rv5_csr_1 (
    .clk(clock), .addr(system_imm), .w_data(ra), .wen(csr_sel), .pc_in({rv5_pcu_1_pc_2, rv5_pcu_1_pc}),
    .ecall_sel(ecall_sel), .mret_sel(mret_sel), .R_DATA(rv5_csr_1_r_data), .MTVEC_OUT(mtvec), .MEPC_OUT(mepc));
  Multiplexer #(.Selector_Bits(5), .Bits(2)) multiplexer_5 (
    .sel(active_ir), .in_0(2'b00), .in_1(2'b00), .in_2(2'b00), .in_3(2'b00), .in_4(2'b00), .in_5(2'b00),
    .in_6(2'b00), .in_7(2'b00), .in_8(2'b00), .in_9(2'b00), .in_10(2'b00), .in_11(2'b00), .in_12(2'b00),
    .in_13(2'b00), .in_14(2'b00), .in_15(2'b00), .in_16(2'b00), .in_17(dr_shift[1:0]), .in_18(2'b00),
    .in_19(2'b00), .in_20(2'b00), .in_21(2'b00), .in_22(2'b00), .in_23(2'b00), .in_24(2'b00), .in_25(2'b00),
    .in_26(2'b00), .in_27(2'b00), .in_28(2'b00), .in_29(2'b00), .in_30(2'b00), .in_31(2'b00),
    .out(update_dr_op));
  // RV5_INSTR_DECODE rv5_instr_decode_1: pin names not known; wires that end beside it: funct7, ROM_d, rs2, rs1, funct3, rd, opcode, UJ_imm_sel, U_imm_sel, S_imm_sel, SB_imm_sel, I_imm_sel, alu_mod, ram_wen, wb_sel
  Multiplexer #(.Selector_Bits(2), .Bits(32)) multiplexer_6 (
    .sel(wb_sel), .in_0(rv5_memory_1_p5), .in_1({add_1_s, 2'b00}), .in_2(rv5_memory_1_p13),
    .in_3(rv5_csr_1_r_data), .out(multiplexer_6_out));
  Multiplexer #(.Selector_Bits(4), .Bits(2)) multiplexer_7 (
    .sel(state_q), .in_0(op), .in_1(op), .in_2(op), .in_3(op), .in_4(op), .in_5(op), .in_6(op), .in_7(op),
    .in_8(op), .in_9(op), .in_10(op), .in_11(op), .in_12(op), .in_13(op), .in_14(op), .in_15(update_dr_op),
    .out(op_d));
  Multiplexer #(.Bits(5)) multiplexer_8 (.sel(ecall_sel), .in_0(rs1), .in_1(5'b01010), .out(multiplexer_8_out));
  Multiplexer #(.Bits(5)) multiplexer_9 (.sel(ecall_sel), .in_0(rs2), .in_1(5'b10001), .out(multiplexer_9_out));
  RV5_GPR rv5_gpr_1 (
    .RS1(multiplexer_8_out), .RS2(multiplexer_9_out), .D_in(multiplexer_6_out), .clk(clock), .WEN(reg_wen),
    .RD(rd), .RA(ra), .RB(rv5_gpr_1_rb));  // open: RD0
  Multiplexer #(.Selector_Bits(5), .Bits(32)) multiplexer_10 (
    .sel(active_ir), .in_0({32{1'b0}}), .in_1({32{1'b0}}), .in_2({32{1'b0}}), .in_3({32{1'b0}}),
    .in_4({32{1'b0}}), .in_5({32{1'b0}}), .in_6({32{1'b0}}), .in_7({32{1'b0}}), .in_8({32{1'b0}}),
    .in_9({32{1'b0}}), .in_10({32{1'b0}}), .in_11({32{1'b0}}), .in_12({32{1'b0}}), .in_13({32{1'b0}}),
    .in_14({32{1'b0}}), .in_15({32{1'b0}}), .in_16({32{1'b0}}),
    .in_17({dr_shift[33:17], dmistat_en, dr_shift[15:2]}), .in_18({32{1'b0}}), .in_19({32{1'b0}}),
    .in_20({32{1'b0}}), .in_21({32{1'b0}}), .in_22({32{1'b0}}), .in_23({32{1'b0}}), .in_24({32{1'b0}}),
    .in_25({32{1'b0}}), .in_26({32{1'b0}}), .in_27({32{1'b0}}), .in_28({32{1'b0}}), .in_29({32{1'b0}}),
    .in_30({32{1'b0}}), .in_31({32{1'b0}}), .out(update_dr_data));
  // RV5_MEMORY rv5_memory_1: pin names not known; wires that end beside it: ram_ren, ecall_sel, alu_op, ram_b, rv5_memory_1_p5, ram_h, rv5_gpr_1_rb, reg_wen, ram_wen, branch_sel, ram_ren, jal_sel, rv5_memory_1_p13, jalr_sel, clock, alu_a_sel, ram_b, ld_signext, ram_h, csr_sel, ld_signext, mret_sel, system_imm
  Multiplexer #(.Selector_Bits(2), .Bits(32)) multiplexer_11 (
    .sel(alu_a_sel), .in_0(ra), .in_1({rv5_pcu_1_pc_2, rv5_pcu_1_pc}), .in_2({32{1'b0}}), .in_3({32{1'b0}}),
    .out(multiplexer_11_out));
  Multiplexer #(.Bits(32)) multiplexer_12 (
    .sel(or_1_out), .in_0(rv5_gpr_1_rb), .in_1(imm_32), .out(multiplexer_12_out));
  or or_1 (or_1_out, I_imm_sel, S_imm_sel, U_imm_sel);
  Multiplexer #(.Selector_Bits(4), .Bits(32)) multiplexer_13 (
    .sel(state_q), .in_0(data), .in_1(data), .in_2(data), .in_3(data), .in_4(data), .in_5(data), .in_6(data),
    .in_7(data), .in_8(data), .in_9(data), .in_10(data), .in_11(data), .in_12(data), .in_13(data),
    .in_14(data), .in_15(update_dr_data), .out(data_d));
  RV5_ALU rv5_alu_1 (
    .OP(alu_op), .Y(rv5_memory_1_p5), .A(multiplexer_11_out), .B(multiplexer_12_out), .BR(br_cond),
    .MOD(alu_mod));
  Multiplexer #(.Selector_Bits(5), .Bits(7)) multiplexer_14 (
    .sel(active_ir), .in_0({7{1'b0}}), .in_1({7{1'b0}}), .in_2({7{1'b0}}), .in_3({7{1'b0}}),
    .in_4({7{1'b0}}), .in_5({7{1'b0}}), .in_6({7{1'b0}}), .in_7({7{1'b0}}), .in_8({7{1'b0}}),
    .in_9({7{1'b0}}), .in_10({7{1'b0}}), .in_11({7{1'b0}}), .in_12({7{1'b0}}), .in_13({7{1'b0}}),
    .in_14({7{1'b0}}), .in_15({7{1'b0}}), .in_16({7{1'b0}}), .in_17(dr_shift[40:34]), .in_18({7{1'b0}}),
    .in_19({7{1'b0}}), .in_20({7{1'b0}}), .in_21({7{1'b0}}), .in_22({7{1'b0}}), .in_23({7{1'b0}}),
    .in_24({7{1'b0}}), .in_25({7{1'b0}}), .in_26({7{1'b0}}), .in_27({7{1'b0}}), .in_28({7{1'b0}}),
    .in_29({7{1'b0}}), .in_30({7{1'b0}}), .in_31({7{1'b0}}), .out(update_dr_addr));
  Multiplexer #(.Selector_Bits(4), .Bits(7)) multiplexer_15 (
    .sel(state_q), .in_0(addr), .in_1(addr), .in_2(addr), .in_3(addr), .in_4(addr), .in_5(addr), .in_6(addr),
    .in_7(addr), .in_8(addr), .in_9(addr), .in_10(addr), .in_11(addr), .in_12(addr), .in_13(addr),
    .in_14(addr), .in_15(update_dr_addr), .out(addr_d));
  Multiplexer #(.Selector_Bits(5), .Bits(2)) multiplexer_16 (
    .sel(active_ir), .in_0(2'b00), .in_1(2'b00), .in_2(2'b00), .in_3(2'b00), .in_4(2'b00), .in_5(2'b00),
    .in_6(2'b00), .in_7(2'b00), .in_8(2'b00), .in_9(2'b00), .in_10(2'b00), .in_11(2'b00), .in_12(2'b00),
    .in_13(2'b00), .in_14(2'b00), .in_15(2'b00), .in_16(2'b00), .in_17(2'b00), .in_18(2'b00), .in_19(2'b00),
    .in_20(2'b00), .in_21(2'b00), .in_22(2'b00), .in_23(2'b00), .in_24(2'b00), .in_25(2'b00), .in_26(2'b00),
    .in_27(2'b00), .in_28(2'b00), .in_29(2'b00), .in_30(2'b00), .in_31(2'b00), .out(update_dr_dmistat));
  Multiplexer #(.Selector_Bits(4), .Bits(2)) multiplexer_17 (
    .sel(state_q), .in_0(dmistat), .in_1(dmistat), .in_2(dmistat), .in_3(dmistat), .in_4(dmistat),
    .in_5(dmistat), .in_6(dmistat), .in_7(dmistat), .in_8(dmistat), .in_9(dmistat), .in_10(dmistat),
    .in_11(dmistat), .in_12(dmistat), .in_13(dmistat), .in_14(dmistat), .in_15(update_dr_dmistat),
    .out(dmistat_d));
  // also tied to GND on the sheet: {addr_d[0], addr_d[1], addr_d[2], addr_d[3], addr_d[4], addr_d[5], addr_d[6], data_d[0], data_d[1], data_d[2], data_d[3], data_d[4], data_d[5], data_d[6], data_d[7], data_d[8], data_d[9], data_d[10], data_d[11], data_d[12], data_d[13], data_d[14], data_d[15], data_d[16], data_d[17], data_d[18], data_d[19], data_d[20], data_d[21], data_d[22], data_d[23], data_d[24], data_d[25], data_d[26], data_d[27], data_d[28], data_d[29], data_d[30], data_d[31], dmistat_d[0], dmistat_d[1]}

  // Other names for the same wires on the sheet: clk = clock; dmi_req = dmi_busy_d; ir_shift[0] = dr_shift[0];
  //   tdo_t = dr_shift[0]; shifted_dr[40:0] = {TDI, dr_shift[40:17], dmistat_en, dr_shift[15:1]};
  //   dr_shift[16] = dmistat_en; shifted_ir[4:0] = {TDI, ir_shift}; data_en = addr_en; op_en = addr_en

  // Notes on the sheet:
  //   clock: Hz: 1000
  //   Things to do:
  //   1. Redesign to make simpler.
  //       * PCU should behave more like
  //          register - adding should happen
  //          outside. This way we can take
  //          the +4 signal.
  //          Also, ALU should not be used
  //          to calculate relative jumps.
  //          This should be a seperate adder.
  //   contents of lookuptable_1 (hex, n*v repeats v):
  //   1,0,1,2,a,3,4,0,5,6,5,6,7,9,7,8,5,9,1,2,b,c,b,c,d,f,d,e,b,f,1,2
  //   This is pure simulator shenanigans.
  //   We have each register enabled
  //   by default and line things up so
  //   that we view what goes into them
  //   as a table indexed by instruction.
  //   Todo:
  //   If dr-shift bit 17 is high and
  //   active IR is 0x10 and we're
  //   in Update DR,
  //   do a hard reset of the DMI.
  //   Here we are trying to make this circuit hierarchical
  //       RV5-REGS contains register bank related hw.
  //       RV5-ALU contains ALU related hw
  //       RV5-INSTR-DECODE contains Instruction Reg, and all needed decodes
  //             decoder for immediate sel
  //       RV5-IMM is a combinatorial that extracts the needed immediates, 
  //              and provides the sign-extended 32-bit value thru a MUX.
  //       RV5-PCU needs some fixes.
  //              increments the PC and allows Jumps, and provides next PC for JAL save of PC.
  //   See examples in Digital in particular processors as to how 
  //   to do this.  
  //   TODO: 
  //   1st. Add a test to each element in the hierarchy.
  //   2nd Resize boxes with appropriate SVG for readable packages w. appropriate signals.
  //   We need to:
  //       RV5-INSTR-DECODE: Decodes the instruction set and provides control signals, and FMT
  //            decode for immediate select has been completed.
  //       Implement:
  //            RV5-LOAD-STORE: Provides Load and Store
  //            RV5-MEMORY: Include ROM and RAM.
  //            RV5-IO: Provides a mean to read a program, communicate with a terminal (keyboard/display)
  //            Create a ROM/RAM  bootstrap
  //                 that loads a program.
  //   Note: Assembler test programs can be found at:   
  //      https://github.com/riscv-software-src/riscv-tests
  //   PCU (Program Control Unit, 
  //   PC = PC + 4, or PC = PC += SBimm32
  //   or PC = ALU out or PC += sgn_ext-imm32
  //   for FMT U, and UJ
  //   Need to figure out a way to load memory
  //   with instructions, ideally from RARS.
  //   Check out how MARS does it for MIPS.
  //   NEXT, NEED LOAD AND STORE,
  //   Address comes from ALU output
  //   which goes to memory via see-thru latch
  //    latch,which goes out to memory for 
  //   loading and storing.  reads 32-word
  //   and stores in rd.   Need to figure out a good
  //   approach to read and write to memory 
  //   with Digital and load it at start up.
  //   We need to arbitrate use of memory 
  //   between load/store and fetching instruction.
  //   RV5-DECODER:
  //      decodes: opcode, funct3, funct7
  //      generates: 
  //           # FMT - DO I NEED IT HERE?
  //           # imm_sel,  DONE ALREADY
  //           wen, 
  //           sub/add, 
  //           func_sel
endmodule
